// Logisim project CPU.circ as structural Verilog
module REG4 (
  input  PR,
  input  CLR,
  input  CLK,
  input  D1,
  input  D2,
  input  D3,
  input  D4,
  output Q1,
  output Q2,
  output Q3,
  output Q4,
  output Q1_NOT,
  output Q2_NOT,
  output Q3_NOT,
  output Q4_NOT
);

  D_Flip_Flop d_ff_1 (.clk(CLK), .D(D1), .Q(Q1), .Qn(Q1_NOT), .preset(PR), .reset(CLR));
  D_Flip_Flop d_ff_2 (.clk(CLK), .D(D2), .Q(Q2), .Qn(Q2_NOT), .preset(PR), .reset(CLR));
  D_Flip_Flop d_ff_3 (.clk(CLK), .D(D3), .Q(Q3), .Qn(Q3_NOT), .preset(PR), .reset(CLR));
  D_Flip_Flop d_ff_4 (.clk(CLK), .D(D4), .Q(Q4), .Qn(Q4_NOT), .preset(PR), .reset(CLR));

  // Notes on the sheet:
  //   Registrador Paralelo
endmodule

module CPU (
);

  wire clock_1_out, K0, K1, K2, K3, L0, L1, L2, L3, L4, L5, L6, L7, L8, L9, S0, S1, S2, S3, S4, S5, S6, S7,
       S8, S9;
  wire [3:0] HEX0, HEX1, HEX2, HEX3, HEX4, HEX5;
  wire [7:0] Contador_q;
  wire [15:0] ROM_data;

  Clock clock_1 (.out(clock_1_out));
  COUNTER8 Contador (.CLK(clock_1_out), .Vcc(1'b1), .Q(Contador_q));  // open: CLR
  ControlUnit Unidade_de_Controle ();
  REG4_Grouped REG1 ();  // open: CLK, D, Q, Q_NOT
  REG16 REG16 (.D(ROM_data), .Clock(clock_1_out), .Q({HEX5, HEX4, HEX3, HEX2}));  // open: Preset, Clear
  ROM #(.dataWidth(16), .Select("low")) ROM (.addr(Contador_q), .data(ROM_data));
  ULA ULA ();  // open: A, B, Op, R
  REG4_Grouped REG2 ();  // open: CLK, D, Q, Q_NOT
  // Digital_Oscilloscope digital_oscilloscope_1: pin names not known
  Hex_Digit_Display hex_digit_display_1 (.value(HEX5));  // open: dp
  LED u_L9 (.in(L9));
  LED u_L8 (.in(L8));
  // DipSwitch #(.NSwitches(1)) S8: pin names not known; wires that end beside it: S8
  // DipSwitch #(.NSwitches(1)) S9: pin names not known; wires that end beside it: S9
  Hex_Digit_Display hex_digit_display_2 (.value(HEX3));  // open: dp
  Hex_Digit_Display hex_digit_display_3 (.value(HEX4));  // open: dp
  LED u_L7 (.in(L7));
  LED u_L6 (.in(L6));
  // DipSwitch #(.NSwitches(1)) S7: pin names not known; wires that end beside it: S7
  // DipSwitch #(.NSwitches(1)) S6: pin names not known; wires that end beside it: S6
  // DipSwitch #(.NSwitches(1)) S5: pin names not known; wires that end beside it: S5
  Hex_Digit_Display hex_digit_display_4 (.value(HEX2));  // open: dp
  LED u_L3 (.in(L3));
  LED u_L5 (.in(L5));
  LED u_L4 (.in(L4));
  // DipSwitch #(.NSwitches(1)) S4: pin names not known; wires that end beside it: S4
  // DipSwitch #(.NSwitches(1)) S3: pin names not known; wires that end beside it: S3
  Hex_Digit_Display hex_digit_display_5 (.value(HEX1));  // open: dp
  Hex_Digit_Display hex_digit_display_6 (.value(HEX0));  // open: dp
  LED u_L1 (.in(L1));
  LED u_L2 (.in(L2));
  LED u_L0 (.in(L0));
  // DipSwitch #(.NSwitches(1)) S0: pin names not known; wires that end beside it: S0
  // DipSwitch #(.NSwitches(1)) S1: pin names not known; wires that end beside it: S1
  // DipSwitch #(.NSwitches(1)) S2: pin names not known; wires that end beside it: S2
  Button u_K2 (.out(K2));
  Button u_K3 (.out(K3));
  Button u_K0 (.out(K0));
  Button u_K1 (.out(K1));

  // Notes on the sheet:
  //   contents of ROM (hex, n*v repeats v):
  //   6005 9101 6202 6304 c08 0 0 0 400 6001 9001 9002 6302 6102 9302 6200 6001 800
endmodule

module COUNTER8 (
  input  CLR,
  input  CLK,
  input  Vcc,
  output [7:0] Q
);

  wire and_6_out, T2, T3, T4, T5, T6;

  T_Flip_Flop t_ff_1 (.clk(CLK), .T(Vcc), .Q(Q[0]), .reset(CLR));  // open: Qn, preset
  T_Flip_Flop t_ff_2 (.clk(CLK), .T(Q[0]), .Q(Q[1]), .reset(CLR));  // open: Qn, preset
  and and_1 (T2, Q[0], Q[1]);
  T_Flip_Flop t_ff_3 (.clk(CLK), .T(T2), .Q(Q[2]), .reset(CLR));  // open: Qn, preset
  and and_2 (T3, T2, Q[2]);
  T_Flip_Flop t_ff_4 (.clk(CLK), .T(T3), .Q(Q[3]), .reset(CLR));  // open: Qn, preset
  and and_3 (T4, T3, Q[3]);
  T_Flip_Flop t_ff_5 (.clk(CLK), .T(T4), .Q(Q[4]), .reset(CLR));  // open: Qn, preset
  and and_4 (T5, T4, Q[4]);
  T_Flip_Flop t_ff_6 (.clk(CLK), .T(T5), .Q(Q[5]), .reset(CLR));  // open: Qn, preset
  and and_5 (T6, T5, Q[5]);
  T_Flip_Flop t_ff_7 (.clk(CLK), .T(T6), .Q(Q[6]), .reset(CLR));  // open: Qn, preset
  and and_6 (and_6_out, T6, Q[6]);
  T_Flip_Flop t_ff_8 (.clk(CLK), .T(and_6_out), .Q(Q[7]), .reset(CLR));  // open: Qn, preset

  // Notes on the sheet:
  //   Contador de 8 Bits Síncrono
endmodule

module ROM16x16 (
  input  Clock,
  output [3:0] Address,
  output [15:0] Word
);

  wire and_1_out, and_2_out, and_3_out, and_4_out, and_5_out, and_6_out, and_7_out, and_8_out, and_9_out,
       and_10_out, and_11_out, and_12_out, and_13_out, and_14_out, and_15_out, and_16_out,
       demultiplexer_1_out0, demultiplexer_1_out1, demultiplexer_1_out2, demultiplexer_1_out3,
       demultiplexer_2_out0, demultiplexer_2_out1, demultiplexer_2_out2, demultiplexer_2_out3;
  wire [3:0] undriven, undriven_2;
  wire [15:0] reg16_1_q, reg16_2_q, reg16_3_q, reg16_4_q, reg16_5_q, reg16_6_q, reg16_7_q, reg16_8_q,
       reg16_9_q, reg16_10_q, reg16_11_q, reg16_12_q, reg16_13_q, reg16_14_q, reg16_15_q, reg16_16_q;

  // DipSwitch A3_A2_A1_A0: pin names not known; wires that end beside it: Address[3], Address[2], Address[1], 1'b1, Address[0]
  Demultiplexer #(.select(2), .enable("false")) demultiplexer_1 (
    .out0(demultiplexer_1_out0), .out1(demultiplexer_1_out1), .out2(demultiplexer_1_out2),
    .out3(demultiplexer_1_out3), .in(1'b1), .sel(Address[1:0]));
  Demultiplexer #(.select(2), .enable("false")) demultiplexer_2 (
    .out0(demultiplexer_2_out0), .out1(demultiplexer_2_out1), .out2(demultiplexer_2_out2),
    .out3(demultiplexer_2_out3), .in(1'b1), .sel(Address[3:2]));
  Hex_Digit_Display hex_digit_display_1 (.value(undriven));  // open: dp
  Hex_Digit_Display hex_digit_display_2 (.value(undriven_2));  // open: dp
  LED led_1 (.in(and_1_out));
  and and_1 (and_1_out, demultiplexer_1_out0, demultiplexer_2_out0);
  REG16 reg16_1 (.D({16{1'b0}}), .Clock(Clock), .Q(reg16_1_q));  // open: Preset, Clear
  LED led_2 (.in(and_2_out));
  and and_2 (and_2_out, demultiplexer_1_out1, demultiplexer_2_out0);
  LED led_3 (.in(and_3_out));
  and and_3 (and_3_out, demultiplexer_1_out2, demultiplexer_2_out0);
  and and_4 (and_4_out, demultiplexer_1_out3, demultiplexer_2_out0);
  assign Word = and_1_out ? reg16_1_q : 16'bz;  // Controlled_Buffer controlled_buffer_1
  assign Word = and_2_out ? reg16_2_q : 16'bz;  // Controlled_Buffer controlled_buffer_2
  REG16 reg16_2 (.D(16'h1), .Clock(Clock), .Q(reg16_2_q));  // open: Preset, Clear
  assign Word = and_3_out ? reg16_3_q : 16'bz;  // Controlled_Buffer controlled_buffer_3
  REG16 reg16_3 (.D(16'h2), .Clock(Clock), .Q(reg16_3_q));  // open: Preset, Clear
  assign Word = and_4_out ? reg16_4_q : 16'bz;  // Controlled_Buffer controlled_buffer_4
  LED led_4 (.in(and_4_out));
  REG16 reg16_4 (.D(16'h3), .Clock(Clock), .Q(reg16_4_q));  // open: Preset, Clear
  LED led_5 (.in(and_5_out));
  and and_5 (and_5_out, demultiplexer_1_out0, demultiplexer_2_out1);
  and and_6 (and_6_out, demultiplexer_1_out1, demultiplexer_2_out1);
  assign Word = and_5_out ? reg16_5_q : 16'bz;  // Controlled_Buffer controlled_buffer_5
  REG16 reg16_5 (.D(16'h4), .Clock(Clock), .Q(reg16_5_q));  // open: Preset, Clear
  assign Word = and_6_out ? reg16_6_q : 16'bz;  // Controlled_Buffer controlled_buffer_6
  LED led_6 (.in(and_6_out));
  REG16 reg16_6 (.D(16'h5), .Clock(Clock), .Q(reg16_6_q));  // open: Preset, Clear
  LED led_7 (.in(and_7_out));
  and and_7 (and_7_out, demultiplexer_1_out2, demultiplexer_2_out1);
  REG16 reg16_7 (.D(16'h6), .Clock(Clock), .Q(reg16_7_q));  // open: Preset, Clear
  LED led_8 (.in(and_8_out));
  and and_8 (and_8_out, demultiplexer_1_out3, demultiplexer_2_out1);
  assign Word = and_7_out ? reg16_7_q : 16'bz;  // Controlled_Buffer controlled_buffer_7
  assign Word = and_8_out ? reg16_8_q : 16'bz;  // Controlled_Buffer controlled_buffer_8
  REG16 reg16_8 (.D(16'h7), .Clock(Clock), .Q(reg16_8_q));  // open: Preset, Clear
  LED led_9 (.in(and_9_out));
  and and_9 (and_9_out, demultiplexer_1_out0, demultiplexer_2_out2);
  REG16 reg16_9 (.D(16'h8), .Clock(Clock), .Q(reg16_9_q));  // open: Preset, Clear
  LED led_10 (.in(and_10_out));
  and and_10 (and_10_out, demultiplexer_1_out1, demultiplexer_2_out2);
  LED led_11 (.in(and_11_out));
  and and_11 (and_11_out, demultiplexer_1_out2, demultiplexer_2_out2);
  and and_12 (and_12_out, demultiplexer_1_out3, demultiplexer_2_out2);
  assign Word = and_9_out ? reg16_9_q : 16'bz;  // Controlled_Buffer controlled_buffer_9
  assign Word = and_10_out ? reg16_10_q : 16'bz;  // Controlled_Buffer controlled_buffer_10
  REG16 reg16_10 (.D(16'h9), .Clock(Clock), .Q(reg16_10_q));  // open: Preset, Clear
  assign Word = and_11_out ? reg16_11_q : 16'bz;  // Controlled_Buffer controlled_buffer_11
  REG16 reg16_11 (.D(16'ha), .Clock(Clock), .Q(reg16_11_q));  // open: Preset, Clear
  assign Word = and_12_out ? reg16_12_q : 16'bz;  // Controlled_Buffer controlled_buffer_12
  LED led_12 (.in(and_12_out));
  REG16 reg16_12 (.D(16'hb), .Clock(Clock), .Q(reg16_12_q));  // open: Preset, Clear
  LED led_13 (.in(and_13_out));
  and and_13 (and_13_out, demultiplexer_1_out0, demultiplexer_2_out3);
  and and_14 (and_14_out, demultiplexer_1_out1, demultiplexer_2_out3);
  assign Word = and_13_out ? reg16_13_q : 16'bz;  // Controlled_Buffer controlled_buffer_13
  REG16 reg16_13 (.D(16'hc), .Clock(Clock), .Q(reg16_13_q));  // open: Preset, Clear
  assign Word = and_14_out ? reg16_14_q : 16'bz;  // Controlled_Buffer controlled_buffer_14
  LED led_14 (.in(and_14_out));
  REG16 reg16_14 (.D(16'hd), .Clock(Clock), .Q(reg16_14_q));  // open: Preset, Clear
  LED led_15 (.in(and_15_out));
  and and_15 (and_15_out, demultiplexer_1_out2, demultiplexer_2_out3);
  REG16 reg16_15 (.D(16'he), .Clock(Clock), .Q(reg16_15_q));  // open: Preset, Clear
  LED led_16 (.in(and_16_out));
  and and_16 (and_16_out, demultiplexer_1_out3, demultiplexer_2_out3);
  assign Word = and_15_out ? reg16_15_q : 16'bz;  // Controlled_Buffer controlled_buffer_15
  assign Word = and_16_out ? reg16_16_q : 16'bz;  // Controlled_Buffer controlled_buffer_16
  REG16 reg16_16 (.D(16'hf), .Clock(Clock), .Q(reg16_16_q));  // open: Preset, Clear

  // Notes on the sheet:
  //   ROM 16x16
  //   Lines
  //   Columns
  //   Line 0
  //   Line 1
  //   Line 2
  //   Line 3
  //   Column 0
  //   Column 1
  //   Column 2
  //   Column 3
endmodule

module REG16 (
  input  Preset,
  input  Clock,
  input  [15:0] D,
  input  Clear,
  output [15:0] Q
);

  REG4 reg4_1 (
    .CLK(Clock), .D1(D[0]), .D2(D[1]), .D3(D[2]), .D4(D[3]), .PR(Preset), .CLR(Clear), .Q1(Q[0]), .Q2(Q[1]),
    .Q3(Q[2]), .Q4(Q[3]));  // open: Q1_NOT, Q2_NOT, Q3_NOT, Q4_NOT
  REG4 reg4_2 (
    .CLK(Clock), .D1(D[4]), .D2(D[5]), .D3(D[6]), .D4(D[7]), .PR(Preset), .CLR(Clear), .Q1(Q[4]), .Q2(Q[5]),
    .Q3(Q[6]), .Q4(Q[7]));  // open: Q1_NOT, Q2_NOT, Q3_NOT, Q4_NOT
  REG4 reg4_3 (
    .CLK(Clock), .D1(D[8]), .D2(D[9]), .D3(D[10]), .D4(D[11]), .PR(Preset), .CLR(Clear), .Q1(Q[8]),
    .Q2(Q[9]), .Q3(Q[10]), .Q4(Q[11]));  // open: Q1_NOT, Q2_NOT, Q3_NOT, Q4_NOT
  REG4 reg4_4 (
    .CLK(Clock), .D1(D[12]), .D2(D[13]), .D3(D[14]), .D4(D[15]), .PR(Preset), .CLR(Clear), .Q1(Q[12]),
    .Q2(Q[13]), .Q3(Q[14]), .Q4(Q[15]));  // open: Q1_NOT, Q2_NOT, Q3_NOT, Q4_NOT

  // Other names for the same wires on the sheet: CLK = Clock; CLR = Clear; PR = Preset
endmodule

module REG4_Grouped (
  input  CLK,
  input  [3:0] D,
  output [3:0] Q,
  output [3:0] Q_NOT
);

  REG4 reg4_1 (
    .CLK(CLK), .D1(D[0]), .D2(D[1]), .D3(D[2]), .D4(D[3]), .Q1(Q[0]), .Q2(Q[1]), .Q3(Q[2]), .Q4(Q[3]),
    .Q1_NOT(Q_NOT[0]), .Q2_NOT(Q_NOT[1]), .Q3_NOT(Q_NOT[2]), .Q4_NOT(Q_NOT[3]));  // open: PR, CLR
endmodule

module ULA (
  input  [3:0] A,
  input  [3:0] B,
  input  [1:0] Op,
  output [3:0] R
);
endmodule
